// Logisim project Busca.circ as structural Verilog: 1 circuit, main circuit main
module main (
  input  clock,
  output [31:0] out_2
);

  wire [31:0] adder_1_out, register_1_q;

  Register #(.width(32)) register_1 (.D(adder_1_out), .en(1'b1), .clk(clock), .Q(register_1_q), .clr(1'b0));
  ROM #(.addrWidth(24), .dataWidth(32)) rom_1 (.addr(register_1_q[25:2]), .data(out_2));
  Adder #(.width(32)) adder_1 (.a(register_1_q), .b(32'h4), .out(adder_1_out), .cin(1'b0));  // open: cout

  // Notes on the sheet:
  //   contents of rom_1 (hex, n*v repeats v):
  //   ab21bab1 21ab21a1 11b1b12e 1131231 c321312c 3b212121 c33121c3 c1233213 31231413 12231231 21312313
  //   3313121c 3b3121 23 12c312c3 1312c c112c3c3 33213c21 21c32121 331312c3 1332123c 321123c1 c3c23c2c
  //   221c3211 3c
endmodule
