// Logisim project aula1.circ as structural Verilog: 3 circuits, main circuit main
module main (
  input  in_1,
  input  in_2,
  output out_3
);

  wire and_1_out, and_2_out, not_1_out, not_2_out;

  not not_1 (not_1_out, in_1);
  not not_2 (not_2_out, in_2);
  and and_1 (and_1_out, not_1_out, in_2);
  and and_2 (and_2_out, in_1, not_2_out);
  or or_1 (out_3, and_1_out, and_2_out);
endmodule

module MUX2x1 (
  input  In0,
  input  In1,
  input  S,
  output mux_out
);

  wire and_1_out, and_2_out, not_1_out;

  not not_1 (not_1_out, S);
  and and_1 (and_1_out, not_1_out, In0);
  and and_2 (and_2_out, S, In1);
  or or_1 (mux_out, and_1_out, and_2_out);
endmodule

module MUX4x1 (
  input  In0,
  input  In1,
  input  In2,
  input  In3,
  input  S0,
  input  S1,
  output mux_out
);

  wire mux2x1_1_mux_out, mux2x1_2_mux_out;

  MUX2x1 mux2x1_1 (.In0(In0), .In1(In1), .S(S0), .mux_out(mux2x1_1_mux_out));
  MUX2x1 mux2x1_2 (.In0(In2), .In1(In3), .S(S0), .mux_out(mux2x1_2_mux_out));
  MUX2x1 mux2x1_3 (.In0(mux2x1_1_mux_out), .In1(mux2x1_2_mux_out), .S(S1), .mux_out(mux_out));
endmodule
