// Logisim project trab1.circ as structural Verilog: 1 circuit, main circuit datapath
module datapath (
  input  ck,
  output [31:0] datapath_out
);

  wire [31:0] adder_1_out, register_1_q;

  Register #(.width(32)) register_1 (.D(adder_1_out), .en(1'b1), .clk(ck), .Q(register_1_q), .clr(1'b0));
  ROM #(.addrWidth(24), .dataWidth(32)) rom_1 (.addr(register_1_q[25:2]), .data(datapath_out));
  Adder #(.width(32)) adder_1 (.a(register_1_q), .b(32'h4), .out(adder_1_out), .cin(1'b0));  // open: cout

  // Notes on the sheet:
  //   PC
  //   contents of rom_1 (hex, n*v repeats v):
  //   0 685 6856 6858 4*0 685 7*0 685 6*0 8 5fd 6*0 5 6*0 8 6*0 85 0 0 ffdf 23523534 56 0 56 0 0 0 5235 3
  //   346346 5 68 4*0 4 6 68 4*0 dd 45 6 85 4*0 dfd 4 0 56 4*0 df 56 0 68 4*0 ff 0 4 85 6*0 5756 566 4*0
  //   ff 0 0 78568 0 0 564 0 f 0 0 885 6 0 0 0 f 0 5 56 0 0 6 0 0 0 8 68 4*0 f 0 0 56685 0 64 0 0 ff 0 0
  //   85 85 0 0 0 f 0 0 6 8 6 0 0 fff 0 0 685 568 0 0 4545 ff 0 0 8585 65555556 455445 4545 0 0 0 8 66 4*0
  //   f 8 56 5dbddfaf 5*0 56 8568 55 68 5*0 68 5688 56 5*0 5 85 5*0 85 0 0 56 8*0 68 0 0 85fff 4*0 85 0 0
  //   0 68568 0 0 5 6 4*0 56 68 6*0 85 8 0 45645645 4*0 56 fd 56 6*0 68df 0 85 5*0 df 85 0 68 4*0 df 0 566
  //   5*0 df 8 85 5*0 68dd 585 5*0 5 f 5*0 68 8 5 4*0 8 565 0 cd 7*0 c 31*0 f 7*0 f 7*0 f 7*0 f 7*0 f 7*0
  //   f 7*0 f 7*0 f 7*0 f 7*0 f 7*0 f 7*0 f 7*0 f 7*0 f 7*0 f 7*0 f 7*0 f 7*0 f
  //   adder
endmodule
