// Logisim project NovoDEMOtipliexadorClk.circ as structural Verilog
module ALU (
  input  [2:0] ALU_ctrl,
  input  [31:0] In0,
  input  [31:0] In1,
  output Zero,
  output [31:0] Outpt
);

  wire or_2_out;
  wire [31:0] adder_1_out, and_1_out, nor_1_out, or_1_out, subtractor_1_out;

  Adder #(.width(32)) adder_1 (.a(In0), .b(In1), .out(adder_1_out), .cin(1'b0));  // open: cout
  Subtractor #(.width(32)) subtractor_1 (.a(In0), .b(In1), .out(subtractor_1_out), .bin(1'b0));  // open: bout
  assign and_1_out = In0 & In1;  // AND_Gate and_1, 32 bits wide
  assign or_1_out = In0 | In1;  // OR_Gate or_1, 32 bits wide
  assign nor_1_out = ~(In0 | In1);  // NOR_Gate nor_1, 32 bits wide
  Multiplexer #(.select(3), .width(32), .enable("false")) multiplexer_1 (
    .in0(adder_1_out), .in1(subtractor_1_out), .in2(and_1_out), .in3(or_1_out), .in4(nor_1_out), .out(Outpt),
    .sel(ALU_ctrl));  // open: in5, in6, in7
  or or_2 (or_2_out, Outpt[15], Outpt[0], Outpt[1], Outpt[2], Outpt[3], Outpt[4], Outpt[5], Outpt[6], Outpt[7], Outpt[8], Outpt[9], Outpt[10], Outpt[11], Outpt[12], Outpt[13], Outpt[14], Outpt[16], Outpt[17], Outpt[18], Outpt[19], Outpt[20], Outpt[21], Outpt[22], Outpt[23], Outpt[24], Outpt[25], Outpt[26], Outpt[27], Outpt[28], Outpt[29], Outpt[30], Outpt[31]);
  not not_1 (Zero, or_2_out);
endmodule

module resgister (
  input  [31:0] DataIn,
  input  [4:0] Reg1,
  input  [4:0] Reg2,
  input  Write,
  input  [4:0] RegWrite,
  input  Clock,
  output [31:0] ReadD1,
  output [31:0] RegD2
);

  wire demultiplexer_1_out0, demultiplexer_1_out1, demultiplexer_1_out2, demultiplexer_1_out3,
       demultiplexer_1_out4, demultiplexer_1_out5, demultiplexer_1_out6, demultiplexer_1_out7,
       demultiplexer_1_out8, demultiplexer_1_out9, demultiplexer_1_out10, demultiplexer_1_out11,
       demultiplexer_1_out12, demultiplexer_1_out13, demultiplexer_1_out14, demultiplexer_1_out15,
       demultiplexer_1_out16, demultiplexer_1_out17, demultiplexer_1_out18, demultiplexer_1_out19,
       demultiplexer_1_out20, demultiplexer_1_out21, demultiplexer_1_out22, demultiplexer_1_out23,
       demultiplexer_1_out24, demultiplexer_1_out25, demultiplexer_1_out26, demultiplexer_1_out27,
       demultiplexer_1_out28, demultiplexer_1_out29, demultiplexer_1_out30, demultiplexer_1_out31;
  wire [31:0] register_1_q, register_2_q, register_3_q, register_4_q, register_5_q, register_6_q,
       register_7_q, register_8_q, register_9_q, register_10_q, register_11_q, register_12_q, register_13_q,
       register_14_q, register_15_q, register_16_q, register_17_q, register_18_q, register_19_q,
       register_20_q, register_21_q, register_22_q, register_23_q, register_25_q, register_26_q,
       register_27_q, register_28_q, register_29_q, register_30_q, register_31_q, register_32_q, undriven;

  Demultiplexer #(.select(5), .enable("false")) demultiplexer_1 (
    .out0(demultiplexer_1_out0), .out1(demultiplexer_1_out1), .out2(demultiplexer_1_out2),
    .out3(demultiplexer_1_out3), .out4(demultiplexer_1_out4), .out5(demultiplexer_1_out5),
    .out6(demultiplexer_1_out6), .out7(demultiplexer_1_out7), .out8(demultiplexer_1_out8),
    .out9(demultiplexer_1_out9), .out10(demultiplexer_1_out10), .out11(demultiplexer_1_out11),
    .out12(demultiplexer_1_out12), .out13(demultiplexer_1_out13), .out14(demultiplexer_1_out14),
    .out15(demultiplexer_1_out15), .out16(demultiplexer_1_out16), .out17(demultiplexer_1_out17),
    .out18(demultiplexer_1_out18), .out19(demultiplexer_1_out19), .out20(demultiplexer_1_out20),
    .out21(demultiplexer_1_out21), .out22(demultiplexer_1_out22), .out23(demultiplexer_1_out23),
    .out24(demultiplexer_1_out24), .out25(demultiplexer_1_out25), .out26(demultiplexer_1_out26),
    .out27(demultiplexer_1_out27), .out28(demultiplexer_1_out28), .out29(demultiplexer_1_out29),
    .out30(demultiplexer_1_out30), .out31(demultiplexer_1_out31), .in(Write), .sel(RegWrite));
  Register #(.width(32)) register_1 (.D(DataIn), .en(demultiplexer_1_out0), .clk(Clock), .Q(register_1_q), .clr(1'b0));
  Register #(.width(32)) register_2 (.D(DataIn), .en(demultiplexer_1_out1), .clk(Clock), .Q(register_2_q), .clr(1'b0));
  Register #(.width(32)) register_3 (.D(DataIn), .en(demultiplexer_1_out2), .clk(Clock), .Q(register_3_q), .clr(1'b0));
  Register #(.width(32)) register_4 (.D(DataIn), .en(demultiplexer_1_out3), .clk(Clock), .Q(register_4_q), .clr(1'b0));
  Register #(.width(32)) register_5 (.D(DataIn), .en(demultiplexer_1_out4), .clk(Clock), .Q(register_5_q), .clr(1'b0));
  Register #(.width(32)) register_6 (.D(DataIn), .en(demultiplexer_1_out5), .clk(Clock), .Q(register_6_q), .clr(1'b0));
  Register #(.width(32)) register_7 (.D(DataIn), .en(demultiplexer_1_out6), .clk(Clock), .Q(register_7_q), .clr(1'b0));
  Register #(.width(32)) register_8 (.D(DataIn), .en(demultiplexer_1_out7), .clk(Clock), .Q(register_8_q), .clr(1'b0));
  Register #(.width(32)) register_9 (.en(demultiplexer_1_out8), .clk(Clock), .Q(register_9_q), .clr(1'b0));  // open: D
  Register #(.width(32)) register_10 (
    .en(demultiplexer_1_out9), .clk(Clock), .Q(register_10_q), .clr(1'b0));  // open: D
  Register #(.width(32)) register_11 (
    .en(demultiplexer_1_out10), .clk(Clock), .Q(register_11_q), .clr(1'b0));  // open: D
  Register #(.width(32)) register_12 (
    .en(demultiplexer_1_out11), .clk(Clock), .Q(register_12_q), .clr(1'b0));  // open: D
  Register #(.width(32)) register_13 (
    .en(demultiplexer_1_out12), .clk(Clock), .Q(register_13_q), .clr(1'b0));  // open: D
  Register #(.width(32)) register_14 (
    .en(demultiplexer_1_out13), .clk(Clock), .Q(register_14_q), .clr(1'b0));  // open: D
  Register #(.width(32)) register_15 (
    .en(demultiplexer_1_out14), .clk(Clock), .Q(register_15_q), .clr(1'b0));  // open: D
  Register #(.width(32)) register_16 (
    .en(demultiplexer_1_out15), .clk(Clock), .Q(register_16_q), .clr(1'b0));  // open: D
  Register #(.width(32)) register_17 (
    .en(demultiplexer_1_out16), .clk(Clock), .Q(register_17_q), .clr(1'b0));  // open: D
  Register #(.width(32)) register_18 (
    .en(demultiplexer_1_out17), .clk(Clock), .Q(register_18_q), .clr(1'b0));  // open: D
  Register #(.width(32)) register_19 (
    .en(demultiplexer_1_out18), .clk(Clock), .Q(register_19_q), .clr(1'b0));  // open: D
  Register #(.width(32)) register_20 (
    .en(demultiplexer_1_out19), .clk(Clock), .Q(register_20_q), .clr(1'b0));  // open: D
  Register #(.width(32)) register_21 (
    .en(demultiplexer_1_out20), .clk(Clock), .Q(register_21_q), .clr(1'b0));  // open: D
  Register #(.width(32)) register_22 (
    .en(demultiplexer_1_out21), .clk(Clock), .Q(register_22_q), .clr(1'b0));  // open: D
  Register #(.width(32)) register_23 (
    .en(demultiplexer_1_out22), .clk(Clock), .Q(register_23_q), .clr(1'b0));  // open: D
  Register #(.width(32)) register_24 (.en(demultiplexer_1_out23), .clk(Clock));  // open: D, Q, clr
  Register #(.width(32)) register_25 (
    .en(demultiplexer_1_out24), .clk(Clock), .Q(register_25_q), .clr(1'b0));  // open: D
  Register #(.width(32)) register_26 (
    .en(demultiplexer_1_out25), .clk(Clock), .Q(register_26_q), .clr(1'b0));  // open: D
  Register #(.width(32)) register_27 (
    .en(demultiplexer_1_out26), .clk(Clock), .Q(register_27_q), .clr(1'b0));  // open: D
  Register #(.width(32)) register_28 (
    .en(demultiplexer_1_out27), .clk(Clock), .Q(register_28_q), .clr(1'b0));  // open: D
  Register #(.width(32)) register_29 (
    .en(demultiplexer_1_out28), .clk(Clock), .Q(register_29_q), .clr(1'b0));  // open: D
  Register #(.width(32)) register_30 (
    .en(demultiplexer_1_out29), .clk(Clock), .Q(register_30_q), .clr(1'b0));  // open: D
  Register #(.width(32)) register_31 (
    .en(demultiplexer_1_out30), .clk(Clock), .Q(register_31_q), .clr(1'b0));  // open: D
  Register #(.width(32)) register_32 (
    .en(demultiplexer_1_out31), .clk(Clock), .Q(register_32_q), .clr(1'b0));  // open: D
  Multiplexer #(.select(5), .width(32), .enable("false")) multiplexer_1 (
    .in0(register_1_q), .in1(register_2_q), .in2(register_3_q), .in3(register_4_q), .in4(register_5_q),
    .in5(register_6_q), .in6(register_7_q), .in7(register_8_q), .in8(register_9_q), .in9(register_10_q),
    .in10(register_11_q), .in11(register_12_q), .in12(register_13_q), .in13(register_14_q),
    .in14(register_15_q), .in15(register_16_q), .in16(register_17_q), .in17(register_18_q),
    .in18(register_19_q), .in19(register_20_q), .in20(register_21_q), .in21(register_22_q),
    .in22(register_23_q), .in23(undriven), .in24(register_25_q), .in25(register_26_q), .in26(register_27_q),
    .in27(register_28_q), .in28(register_29_q), .in29(register_30_q), .in30(register_31_q),
    .in31(register_32_q), .out(ReadD1), .sel(Reg1));
  Multiplexer #(.select(5), .width(32), .enable("false")) multiplexer_2 (
    .in0(register_1_q), .in1(register_2_q), .in2(register_3_q), .in3(register_4_q), .in4(register_5_q),
    .in5(register_6_q), .in6(register_7_q), .in7(register_8_q), .in8(register_9_q), .in9(register_10_q),
    .in10(register_11_q), .in11(register_12_q), .in12(register_13_q), .in13(register_14_q),
    .in14(register_15_q), .in15(register_16_q), .in16(register_17_q), .in17(register_18_q),
    .in18(register_19_q), .in19(register_20_q), .in20(register_21_q), .in21(register_22_q),
    .in22(register_23_q), .in23(undriven), .in24(register_25_q), .in25(register_26_q), .in26(register_27_q),
    .in27(register_28_q), .in28(register_29_q), .in29(register_30_q), .in30(register_31_q),
    .in31(register_32_q), .out(RegD2), .sel(Reg2));
endmodule
