// Logisim project ALU.circ as structural Verilog
module Registers (
  input  [4:0] Read_1,
  input  [4:0] Read_2,
  input  [31:0] Data,
  output [31:0] out_4,
  output [31:0] out_5
);

  wire [31:0] register_1_q, register_2_q, register_3_q, register_4_q, register_5_q, register_6_q,
       register_7_q, register_8_q, register_9_q, register_10_q, register_11_q, register_12_q, register_13_q,
       register_14_q, register_15_q, register_16_q, register_17_q, register_18_q, register_19_q,
       register_20_q, register_21_q, register_22_q, register_23_q, register_24_q, register_25_q,
       register_26_q, register_27_q, register_28_q, register_29_q, register_30_q, register_31_q,
       register_32_q;

  Register #(.width(32)) register_1 (.Q(register_1_q));  // open: D, en, clk, clr
  Register #(.width(32)) register_2 (.Q(register_2_q));  // open: D, en, clk, clr
  Register #(.width(32)) register_3 (.Q(register_3_q));  // open: D, en, clk, clr
  Register #(.width(32)) register_4 (.Q(register_4_q));  // open: D, en, clk, clr
  Register #(.width(32)) register_5 (.D(Data), .Q(register_5_q));  // open: en, clk, clr
  Register #(.width(32)) register_6 (.D(Data), .Q(register_6_q));  // open: en, clk, clr
  Register #(.width(32)) register_7 (.D(Data), .Q(register_7_q));  // open: en, clk, clr
  Register #(.width(32)) register_8 (.D(Data), .Q(register_8_q));  // open: en, clk, clr
  Register #(.width(32)) register_9 (.Q(register_9_q));  // open: D, en, clk, clr
  Register #(.width(32)) register_10 (.Q(register_10_q));  // open: D, en, clk, clr
  Register #(.width(32)) register_11 (.Q(register_11_q));  // open: D, en, clk, clr
  Register #(.width(32)) register_12 (.Q(register_12_q));  // open: D, en, clk, clr
  Register #(.width(32)) register_13 (.Q(register_13_q));  // open: D, en, clk, clr
  Register #(.width(32)) register_14 (.Q(register_14_q));  // open: D, en, clk, clr
  Register #(.width(32)) register_15 (.Q(register_15_q));  // open: D, en, clk, clr
  Register #(.width(32)) register_16 (.Q(register_16_q));  // open: D, en, clk, clr
  Register #(.width(32)) register_17 (.Q(register_17_q));  // open: D, en, clk, clr
  Register #(.width(32)) register_18 (.Q(register_18_q));  // open: D, en, clk, clr
  Register #(.width(32)) register_19 (.Q(register_19_q));  // open: D, en, clk, clr
  Register #(.width(32)) register_20 (.Q(register_20_q));  // open: D, en, clk, clr
  Register #(.width(32)) register_21 (.Q(register_21_q));  // open: D, en, clk, clr
  Register #(.width(32)) register_22 (.Q(register_22_q));  // open: D, en, clk, clr
  Register #(.width(32)) register_23 (.Q(register_23_q));  // open: D, en, clk, clr
  Register #(.width(32)) register_24 (.Q(register_24_q));  // open: D, en, clk, clr
  Register #(.width(32)) register_25 (.Q(register_25_q));  // open: D, en, clk, clr
  Register #(.width(32)) register_26 (.Q(register_26_q));  // open: D, en, clk, clr
  Register #(.width(32)) register_27 (.Q(register_27_q));  // open: D, en, clk, clr
  Register #(.width(32)) register_28 (.Q(register_28_q));  // open: D, en, clk, clr
  Register #(.width(32)) register_29 (.Q(register_29_q));  // open: D, en, clk, clr
  Register #(.width(32)) register_30 (.Q(register_30_q));  // open: D, en, clk, clr
  Register #(.width(32)) register_31 (.Q(register_31_q));  // open: D, en, clk, clr
  Register #(.width(32)) register_32 (.Q(register_32_q));  // open: D, en, clk, clr
  Multiplexer #(.select(5), .width(32), .enable("false")) multiplexer_1 (
    .in0(register_1_q), .in1(register_2_q), .in2(register_3_q), .in3(register_4_q), .in4(register_5_q),
    .in5(register_6_q), .in6(register_7_q), .in7(register_8_q), .in8(register_9_q), .in9(register_10_q),
    .in10(register_11_q), .in11(register_12_q), .in12(register_13_q), .in13(register_14_q),
    .in14(register_15_q), .in15(register_16_q), .in16(register_17_q), .in17(register_18_q),
    .in18(register_19_q), .in19(register_20_q), .in20(register_21_q), .in21(register_22_q),
    .in22(register_23_q), .in23(register_24_q), .in24(register_25_q), .in25(register_26_q),
    .in26(register_27_q), .in27(register_28_q), .in28(register_29_q), .in29(register_30_q),
    .in30(register_31_q), .in31(register_32_q), .out(out_4), .sel(Read_1));
  Multiplexer #(.select(5), .width(32), .enable("false")) multiplexer_2 (
    .in0(register_1_q), .in1(register_2_q), .in2(register_3_q), .in3(register_4_q), .in4(register_5_q),
    .in5(register_6_q), .in6(register_7_q), .in7(register_8_q), .in8(register_9_q), .in9(register_10_q),
    .in10(register_11_q), .in11(register_12_q), .in12(register_13_q), .in13(register_14_q),
    .in14(register_15_q), .in15(register_16_q), .in16(register_17_q), .in17(register_18_q),
    .in18(register_19_q), .in19(register_20_q), .in20(register_21_q), .in21(register_22_q),
    .in22(register_23_q), .in23(register_24_q), .in24(register_25_q), .in25(register_26_q),
    .in26(register_27_q), .in27(register_28_q), .in28(register_29_q), .in29(register_30_q),
    .in30(register_31_q), .in31(register_32_q), .out(out_5), .sel(Read_2));
endmodule

module ALU (
  input  [2:0] ALU_ctrl,
  input  [31:0] In0,
  input  [31:0] In1,
  output Zero,
  output [31:0] Outpt
);

  wire or_2_out;
  wire [31:0] adder_1_out, and_1_out, nor_1_out, or_1_out, subtractor_1_out;

  Adder #(.width(32)) adder_1 (.a(In0), .b(In1), .out(adder_1_out), .cin(1'b0));  // open: cout
  Subtractor #(.width(32)) subtractor_1 (.a(In0), .b(In1), .out(subtractor_1_out), .bin(1'b0));  // open: bout
  assign and_1_out = In0 & In1;  // AND_Gate and_1, 32 bits wide
  assign or_1_out = In0 | In1;  // OR_Gate or_1, 32 bits wide
  assign nor_1_out = ~(In0 | In1);  // NOR_Gate nor_1, 32 bits wide
  Multiplexer #(.select(3), .width(32), .enable("false")) multiplexer_1 (
    .in0(adder_1_out), .in1(subtractor_1_out), .in2(and_1_out), .in3(or_1_out), .in4(nor_1_out), .out(Outpt),
    .sel(ALU_ctrl));  // open: in5, in6, in7
  or or_2 (or_2_out, Outpt[15], Outpt[0], Outpt[1], Outpt[2], Outpt[3], Outpt[4], Outpt[5], Outpt[6], Outpt[7], Outpt[8], Outpt[9], Outpt[10], Outpt[11], Outpt[12], Outpt[13], Outpt[14], Outpt[16], Outpt[17], Outpt[18], Outpt[19], Outpt[20], Outpt[21], Outpt[22], Outpt[23], Outpt[24], Outpt[25], Outpt[26], Outpt[27], Outpt[28], Outpt[29], Outpt[30], Outpt[31]);
  not not_1 (Zero, or_2_out);
endmodule
