// Logisim project Registradores-aula.circ as structural Verilog: 2 circuits, main circuit main
module main (
);

  registers registers_1 ();  // open: ReadData, ReadRegister0, out_5, ReadRegister1, in_1
endmodule

module registers (
  input  [31:0] in_1,
  input  [4:0] ReadRegister0,
  input  [4:0] ReadRegister1,
  output [31:0] ReadData,
  output [31:0] out_5
);

  wire [31:0] register_1_q, register_2_q, register_3_q, register_4_q, register_5_q, register_6_q,
       register_7_q, register_8_q, register_9_q, register_10_q, register_11_q, register_12_q, register_13_q,
       register_14_q, register_15_q, register_16_q, register_17_q, register_18_q, register_19_q,
       register_20_q, register_21_q, register_22_q, register_23_q, register_25_q, register_26_q,
       register_27_q, register_28_q, register_29_q, register_30_q, register_31_q, undriven, undriven_2;

  Register #(.width(32)) register_1 (.D(in_1), .Q(register_1_q), .clr(1'b0));  // open: en, clk
  Register #(.width(32)) register_2 (.D(in_1), .Q(register_2_q), .clr(1'b0));  // open: en, clk
  Register #(.width(32)) register_3 (.D(in_1), .Q(register_3_q), .clr(1'b0));  // open: en, clk
  Register #(.width(32)) register_4 (.D(in_1), .Q(register_4_q), .clr(1'b0));  // open: en, clk
  Register #(.width(32)) register_5 (.D(in_1), .Q(register_5_q), .clr(1'b0));  // open: en, clk
  Register #(.width(32)) register_6 (.D(in_1), .Q(register_6_q), .clr(1'b0));  // open: en, clk
  Register #(.width(32)) register_7 (.D(in_1), .Q(register_7_q), .clr(1'b0));  // open: en, clk
  Register #(.width(32)) register_8 (.D(in_1), .Q(register_8_q), .clr(1'b0));  // open: en, clk
  Register #(.width(32)) register_9 (.Q(register_9_q), .clr(1'b0));  // open: D, en, clk
  Register #(.width(32)) register_10 (.Q(register_10_q), .clr(1'b0));  // open: D, en, clk
  Register #(.width(32)) register_11 (.Q(register_11_q), .clr(1'b0));  // open: D, en, clk
  Register #(.width(32)) register_12 (.Q(register_12_q), .clr(1'b0));  // open: D, en, clk
  Register #(.width(32)) register_13 (.Q(register_13_q), .clr(1'b0));  // open: D, en, clk
  Register #(.width(32)) register_14 (.Q(register_14_q), .clr(1'b0));  // open: D, en, clk
  Register #(.width(32)) register_15 (.Q(register_15_q), .clr(1'b0));  // open: D, en, clk
  Register #(.width(32)) register_16 (.Q(register_16_q), .clr(1'b0));  // open: D, en, clk
  Register #(.width(32)) register_17 (.Q(register_17_q), .clr(1'b0));  // open: D, en, clk
  Register #(.width(32)) register_18 (.Q(register_18_q), .clr(1'b0));  // open: D, en, clk
  Register #(.width(32)) register_19 (.Q(register_19_q), .clr(1'b0));  // open: D, en, clk
  Register #(.width(32)) register_20 (.Q(register_20_q), .clr(1'b0));  // open: D, en, clk
  Register #(.width(32)) register_21 (.Q(register_21_q), .clr(1'b0));  // open: D, en, clk
  Register #(.width(32)) register_22 (.Q(register_22_q), .clr(1'b0));  // open: D, en, clk
  Register #(.width(32)) register_23 (.Q(register_23_q), .clr(1'b0));  // open: D, en, clk
  Register #(.width(32)) register_24 ();  // open: D, en, Q, clk, clr
  Register #(.width(32)) register_25 (.Q(register_25_q), .clr(1'b0));  // open: D, en, clk
  Register #(.width(32)) register_26 (.Q(register_26_q), .clr(1'b0));  // open: D, en, clk
  Register #(.width(32)) register_27 (.Q(register_27_q), .clr(1'b0));  // open: D, en, clk
  Register #(.width(32)) register_28 (.Q(register_28_q), .clr(1'b0));  // open: D, en, clk
  Register #(.width(32)) register_29 (.Q(register_29_q), .clr(1'b0));  // open: D, en, clk
  Register #(.width(32)) register_30 (.Q(register_30_q), .clr(1'b0));  // open: D, en, clk
  Register #(.width(32)) register_31 (.Q(register_31_q), .clr(1'b0));  // open: D, en, clk
  Register #(.width(32)) register_32 ();  // open: D, en, Q, clk, clr
  Multiplexer #(.select(5), .width(32), .enable("false")) multiplexer_1 (
    .in0(register_1_q), .in1(register_2_q), .in2(register_3_q), .in3(register_4_q), .in4(register_5_q),
    .in5(register_6_q), .in6(register_7_q), .in7(register_8_q), .in8(register_9_q), .in9(register_10_q),
    .in10(register_11_q), .in11(register_12_q), .in12(register_13_q), .in13(register_14_q),
    .in14(register_15_q), .in15(register_16_q), .in16(register_17_q), .in17(register_18_q),
    .in18(register_19_q), .in19(register_20_q), .in20(register_21_q), .in21(register_22_q),
    .in22(register_23_q), .in23(undriven), .in24(register_25_q), .in25(register_26_q), .in26(register_27_q),
    .in27(register_28_q), .in28(register_29_q), .in29(register_30_q), .in30(register_31_q),
    .in31(undriven_2), .out(ReadData), .sel(ReadRegister0));
  Multiplexer #(.select(5), .width(32), .enable("false")) multiplexer_2 (
    .in0(register_1_q), .in1(register_2_q), .in2(register_3_q), .in3(register_4_q), .in4(register_5_q),
    .in5(register_6_q), .in6(register_7_q), .in7(register_8_q), .in8(register_9_q), .in9(register_10_q),
    .in10(register_11_q), .in11(register_12_q), .in12(register_13_q), .in13(register_14_q),
    .in14(register_15_q), .in15(register_16_q), .in16(register_17_q), .in17(register_18_q),
    .in18(register_19_q), .in19(register_20_q), .in20(register_21_q), .in21(register_22_q),
    .in22(register_23_q), .in23(undriven), .in24(register_25_q), .in25(register_26_q), .in26(register_27_q),
    .in27(register_28_q), .in28(register_29_q), .in29(register_30_q), .in30(register_31_q),
    .in31(undriven_2), .out(out_5), .sel(ReadRegister1));
endmodule
