// Logisim project trab2.circ as structural Verilog: 3 circuits, main circuit main
module main (
);

  registers registers_1 ();  // open: ReadRegister0, ReadData, out_6, ReadRegister1, in_1, in_4
endmodule

module registers (
  input  [31:0] in_1,
  input  [4:0] ReadRegister0,
  input  [4:0] ReadRegister1,
  input  [4:0] in_4,
  output [31:0] ReadData,
  output [31:0] out_6
);

  wire demultiplexer_1_out0, demultiplexer_1_out1, demultiplexer_1_out2, demultiplexer_1_out3,
       demultiplexer_1_out4, demultiplexer_1_out5, demultiplexer_1_out6, demultiplexer_1_out7,
       demultiplexer_1_out8, demultiplexer_1_out9, demultiplexer_1_out10, demultiplexer_1_out11,
       demultiplexer_1_out12, demultiplexer_1_out13, demultiplexer_1_out14, demultiplexer_1_out15;
  wire [31:0] register_1_q, register_2_q, register_3_q, register_4_q, register_5_q, register_6_q,
       register_7_q, register_8_q, register_9_q, register_10_q, register_11_q, register_12_q, register_13_q,
       register_14_q, register_15_q, register_16_q, register_17_q, register_18_q, register_19_q,
       register_20_q, register_21_q, register_22_q, register_23_q, register_24_p3, register_25_q,
       register_26_q, register_27_q, register_28_q, register_29_q, register_30_q, register_31_q, undriven;

  Demultiplexer #(.select(5), .enable("false")) demultiplexer_1 (
    .out0(demultiplexer_1_out0), .out1(demultiplexer_1_out1), .out2(demultiplexer_1_out2),
    .out3(demultiplexer_1_out3), .out4(demultiplexer_1_out4), .out5(demultiplexer_1_out5),
    .out6(demultiplexer_1_out6), .out7(demultiplexer_1_out7), .out8(demultiplexer_1_out8),
    .out9(demultiplexer_1_out9), .out10(demultiplexer_1_out10), .out11(demultiplexer_1_out11),
    .out12(demultiplexer_1_out12), .out13(demultiplexer_1_out13), .out14(demultiplexer_1_out14),
    .out15(demultiplexer_1_out15), .in(1'b1), .sel(in_4));  // open: out16, out17, out18, out19, out20, out21, out22, out23, out24, out25, out26, out27, out28, out29, out30, out31
  Register #(.width(32)) register_1 (.D(in_1), .en(demultiplexer_1_out0), .Q(register_1_q), .clr(1'b0));  // open: clk
  Register #(.width(32)) register_2 (.D(in_1), .en(demultiplexer_1_out1), .Q(register_2_q), .clr(1'b0));  // open: clk
  Register #(.width(32)) register_3 (.D(in_1), .en(demultiplexer_1_out2), .Q(register_3_q), .clr(1'b0));  // open: clk
  Register #(.width(32)) register_4 (.D(in_1), .en(demultiplexer_1_out3), .Q(register_4_q), .clr(1'b0));  // open: clk
  Register #(.width(32)) register_5 (.D(in_1), .en(demultiplexer_1_out4), .Q(register_5_q), .clr(1'b0));  // open: clk
  Register #(.width(32)) register_6 (.D(in_1), .en(demultiplexer_1_out5), .Q(register_6_q), .clr(1'b0));  // open: clk
  Register #(.width(32)) register_7 (.D(in_1), .en(demultiplexer_1_out6), .Q(register_7_q), .clr(1'b0));  // open: clk
  Register #(.width(32)) register_8 (.D(in_1), .en(demultiplexer_1_out7), .Q(register_8_q), .clr(1'b0));  // open: clk
  Register #(.width(32)) register_9 (.D(in_1), .en(demultiplexer_1_out8), .Q(register_9_q), .clr(1'b0));  // open: clk
  Register #(.width(32)) register_10 (.D(in_1), .en(demultiplexer_1_out9), .Q(register_10_q), .clr(1'b0));  // open: clk
  Register #(.width(32)) register_11 (
    .D(in_1), .en(demultiplexer_1_out10), .Q(register_11_q), .clr(1'b0));  // open: clk
  Register #(.width(32)) register_12 (
    .D(in_1), .en(demultiplexer_1_out11), .Q(register_12_q), .clr(1'b0));  // open: clk
  Register #(.width(32)) register_13 (
    .D(in_1), .en(demultiplexer_1_out12), .Q(register_13_q), .clr(1'b0));  // open: clk
  Register #(.width(32)) register_14 (
    .D(in_1), .en(demultiplexer_1_out13), .Q(register_14_q), .clr(1'b0));  // open: clk
  Register #(.width(32)) register_15 (
    .D(in_1), .en(demultiplexer_1_out14), .Q(register_15_q), .clr(1'b0));  // open: clk
  Register #(.width(32)) register_16 (
    .D(in_1), .en(demultiplexer_1_out15), .Q(register_16_q), .clr(1'b0));  // open: clk
  Register #(.width(32)) register_17 (.D(in_1), .Q(register_17_q), .clr(1'b0));  // open: en, clk
  Register #(.width(32)) register_18 (.D(in_1), .Q(register_18_q), .clr(1'b0));  // open: en, clk
  Register #(.width(32)) register_19 (.D(in_1), .Q(register_19_q), .clr(1'b0));  // open: en, clk
  Register #(.width(32)) register_20 (.D(in_1), .Q(register_20_q), .clr(1'b0));  // open: en, clk
  Register #(.width(32)) register_21 (.D(in_1), .Q(register_21_q), .clr(1'b0));  // open: en, clk
  Register #(.width(32)) register_22 (.D(in_1), .Q(register_22_q), .clr(1'b0));  // open: en, clk
  Register #(.width(32)) register_23 (.D(in_1), .Q(register_23_q), .clr(1'b0));  // open: en, clk
  // Register #(.width(32)) register_24: pin names not known; wires that end beside it: in_1, 1'b0, register_24_p3
  Register #(.width(32)) register_25 (.D(in_1), .Q(register_25_q), .clr(1'b0));  // open: en, clk
  Register #(.width(32)) register_26 (.D(in_1), .Q(register_26_q), .clr(1'b0));  // open: en, clk
  Register #(.width(32)) register_27 (.D(in_1), .Q(register_27_q), .clr(1'b0));  // open: en, clk
  Register #(.width(32)) register_28 (.D(in_1), .Q(register_28_q), .clr(1'b0));  // open: en, clk
  Register #(.width(32)) register_29 (.D(in_1), .Q(register_29_q), .clr(1'b0));  // open: en, clk
  Register #(.width(32)) register_30 (.D(in_1), .Q(register_30_q), .clr(1'b0));  // open: en, clk
  Register #(.width(32)) register_31 (.D(in_1), .Q(register_31_q), .clr(1'b0));  // open: en, clk
  Register #(.width(32)) register_32 (.D(in_1), .clr(1'b0));  // open: en, clk, Q
  Multiplexer #(.select(5), .width(32), .enable("false")) multiplexer_1 (
    .in0(register_1_q), .in1(register_2_q), .in2(register_3_q), .in3(register_4_q), .in4(register_5_q),
    .in5(register_6_q), .in6(register_7_q), .in7(register_8_q), .in8(register_9_q), .in9(register_10_q),
    .in10(register_11_q), .in11(register_12_q), .in12(register_13_q), .in13(register_14_q),
    .in14(register_15_q), .in15(register_16_q), .in16(register_17_q), .in17(register_18_q),
    .in18(register_19_q), .in19(register_20_q), .in20(register_21_q), .in21(register_22_q),
    .in22(register_23_q), .in23(register_24_p3), .in24(register_25_q), .in25(register_26_q),
    .in26(register_27_q), .in27(register_28_q), .in28(register_29_q), .in29(register_30_q),
    .in30(register_31_q), .in31(undriven), .out(ReadData), .sel(ReadRegister0));
  Multiplexer #(.select(5), .width(32), .enable("false")) multiplexer_2 (
    .in0(register_1_q), .in1(register_2_q), .in2(register_3_q), .in3(register_4_q), .in4(register_5_q),
    .in5(register_6_q), .in6(register_7_q), .in7(register_8_q), .in8(register_9_q), .in9(register_10_q),
    .in10(register_11_q), .in11(register_12_q), .in12(register_13_q), .in13(register_14_q),
    .in14(register_15_q), .in15(register_16_q), .in16(register_17_q), .in17(register_18_q),
    .in18(register_19_q), .in19(register_20_q), .in20(register_21_q), .in21(register_22_q),
    .in22(register_23_q), .in23(register_24_p3), .in24(register_25_q), .in25(register_26_q),
    .in26(register_27_q), .in27(register_28_q), .in28(register_29_q), .in29(register_30_q),
    .in30(register_31_q), .in31(undriven), .out(out_6), .sel(ReadRegister1));
endmodule

module ALU (
  input  [2:0] ALU_ctrl,
  input  [31:0] In0,
  input  [31:0] In1,
  output Zero,
  output [31:0] Outpt
);

  wire or_2_out;
  wire [31:0] adder_1_out, and_1_out, nor_1_out, or_1_out, subtractor_1_out;

  Adder #(.width(32)) adder_1 (.a(In0), .b(In1), .out(adder_1_out), .cin(1'b0));  // open: cout
  Subtractor #(.width(32)) subtractor_1 (.a(In0), .b(In1), .out(subtractor_1_out), .bin(1'b0));  // open: bout
  assign and_1_out = In0 & In1;  // AND_Gate and_1, 32 bits wide
  assign or_1_out = In0 | In1;  // OR_Gate or_1, 32 bits wide
  assign nor_1_out = ~(In0 | In1);  // NOR_Gate nor_1, 32 bits wide
  Multiplexer #(.select(3), .width(32), .enable("false")) multiplexer_1 (
    .in0(adder_1_out), .in1(subtractor_1_out), .in2(and_1_out), .in3(or_1_out), .in4(nor_1_out), .out(Outpt),
    .sel(ALU_ctrl));  // open: in5, in6, in7
  or or_2 (or_2_out, Outpt[15], Outpt[0], Outpt[1], Outpt[2], Outpt[3], Outpt[4], Outpt[5], Outpt[6], Outpt[7], Outpt[8], Outpt[9], Outpt[10], Outpt[11], Outpt[12], Outpt[13], Outpt[14], Outpt[16], Outpt[17], Outpt[18], Outpt[19], Outpt[20], Outpt[21], Outpt[22], Outpt[23], Outpt[24], Outpt[25], Outpt[26], Outpt[27], Outpt[28], Outpt[29], Outpt[30], Outpt[31]);
  not not_1 (Zero, or_2_out);
endmodule
