// Logisim project SignalShift.circ as structural Verilog: 2 circuits, main circuit Signal_Extender
module Signal_Extender (
  input  [15:0] in_16,
  output [31:0] out_32
);


  assign out_32 = {{17{in_16[15]}}, in_16[14:0]};
endmodule

module Shift2 (
  input  [31:0] Sh_in,
  output [31:0] Sh_out
);


  assign Sh_out = {Sh_in[29:0], 2'b00};
endmodule
