// Logisim project ALU__Control.circ as structural Verilog
module ALU_control (
  input  [5:0] Instruction,
  input  [2:0] ALU_op,
  output [5:0] ALU_code
);

  wire [5:0] undriven, undriven_2, undriven_3, undriven_4, undriven_5, undriven_6, undriven_7;

  Multiplexer #(.select(3), .width(6), .enable("false")) multiplexer_1 (
    .in0(undriven), .in1(undriven_2), .in2(undriven_3), .in3(undriven_4), .in4(undriven_5), .in5(undriven_6),
    .in6(undriven_7), .in7(Instruction), .out(ALU_code), .sel(ALU_op));
endmodule
