// Logisim project trab5.circ as structural Verilog: 12 circuits, main circuit trab1_Datapath
module trab1_Datapath (
  input  [31:0] PC,
  input  ck,
  output [31:0] add_out,
  output [31:0] datapath_out
);

  wire [31:0] register_1_q;

  Register #(.width(32)) register_1 (.D(PC), .en(1'b1), .clk(ck), .Q(register_1_q), .clr(1'b0));
  ROM #(.addrWidth(24), .dataWidth(32)) rom_1 (.addr(register_1_q[25:2]), .data(datapath_out));
  // Probe on register_1_q[25:2]
  Adder #(.width(32)) adder_1 (.a(register_1_q), .b(32'h4), .out(add_out), .cin(1'b0));  // open: cout

  // Notes on the sheet:
  //   PC
  //   contents of rom_1 (hex, n*v repeats v):
  //   cffffff 3c01ffff 221824 221825 221827 30230003 34230003 24230003 20230003 221823 3c011001 a0230003
  //   a4230003 ac230003 8c230003 94230003 90230003 0 3e00008 10*0 80000004 4*0 80000004 0 8000004
  //   adder
endmodule

module trab2_Registers (
  input  [4:0] ReadRegister1,
  input  [31:0] WriteData,
  input  [4:0] ReadRegister2,
  input  Write,
  input  [4:0] WriteRegister,
  input  Clock,
  output [31:0] ReadData1,
  output [31:0] ReadData2
);

  wire demultiplexer_1_out0, demultiplexer_1_out1, demultiplexer_1_out2, demultiplexer_1_out3,
       demultiplexer_1_out4, demultiplexer_1_out5, demultiplexer_1_out6, demultiplexer_1_out7,
       demultiplexer_1_out8, demultiplexer_1_out9, demultiplexer_1_out10, demultiplexer_1_out11,
       demultiplexer_1_out12, demultiplexer_1_out13, demultiplexer_1_out14, demultiplexer_1_out15,
       demultiplexer_1_out16, demultiplexer_1_out17, demultiplexer_1_out18, demultiplexer_1_out19,
       demultiplexer_1_out20, demultiplexer_1_out21, demultiplexer_1_out22, demultiplexer_1_out23,
       demultiplexer_1_out24, demultiplexer_1_out25, demultiplexer_1_out26, demultiplexer_1_out27,
       demultiplexer_1_out28, demultiplexer_1_out29, demultiplexer_1_out30, demultiplexer_1_out31;
  wire [31:0] register_1_q, register_2_q, register_3_q, register_4_q, register_5_q, register_6_q,
       register_7_q, register_8_q, register_9_q, register_10_q, register_11_q, register_12_q, register_13_q,
       register_14_q, register_15_q, register_16_q, register_17_q, register_18_q, register_19_q,
       register_20_q, register_21_q, register_22_q, register_23_q, register_24_q, register_25_q,
       register_26_q, register_27_q, register_28_q, register_29_q, register_30_q, register_31_q,
       register_32_q;

  Demultiplexer #(.select(5), .enable("false")) demultiplexer_1 (
    .out0(demultiplexer_1_out0), .out1(demultiplexer_1_out1), .out2(demultiplexer_1_out2),
    .out3(demultiplexer_1_out3), .out4(demultiplexer_1_out4), .out5(demultiplexer_1_out5),
    .out6(demultiplexer_1_out6), .out7(demultiplexer_1_out7), .out8(demultiplexer_1_out8),
    .out9(demultiplexer_1_out9), .out10(demultiplexer_1_out10), .out11(demultiplexer_1_out11),
    .out12(demultiplexer_1_out12), .out13(demultiplexer_1_out13), .out14(demultiplexer_1_out14),
    .out15(demultiplexer_1_out15), .out16(demultiplexer_1_out16), .out17(demultiplexer_1_out17),
    .out18(demultiplexer_1_out18), .out19(demultiplexer_1_out19), .out20(demultiplexer_1_out20),
    .out21(demultiplexer_1_out21), .out22(demultiplexer_1_out22), .out23(demultiplexer_1_out23),
    .out24(demultiplexer_1_out24), .out25(demultiplexer_1_out25), .out26(demultiplexer_1_out26),
    .out27(demultiplexer_1_out27), .out28(demultiplexer_1_out28), .out29(demultiplexer_1_out29),
    .out30(demultiplexer_1_out30), .out31(demultiplexer_1_out31), .in(Write), .sel(WriteRegister));
  Register #(.width(32)) register_1 (
    .D(WriteData), .en(demultiplexer_1_out0), .clk(Clock), .Q(register_1_q), .clr(1'b1));
  Register #(.width(32)) register_2 (
    .D(WriteData), .en(demultiplexer_1_out1), .clk(Clock), .Q(register_2_q), .clr(1'b0));
  Register #(.width(32)) register_3 (
    .D(WriteData), .en(demultiplexer_1_out2), .clk(Clock), .Q(register_3_q), .clr(1'b0));
  Register #(.width(32)) register_4 (
    .D(WriteData), .en(demultiplexer_1_out3), .clk(Clock), .Q(register_4_q), .clr(1'b0));
  Register #(.width(32)) register_5 (
    .D(WriteData), .en(demultiplexer_1_out4), .clk(Clock), .Q(register_5_q), .clr(1'b0));
  Register #(.width(32)) register_6 (
    .D(WriteData), .en(demultiplexer_1_out5), .clk(Clock), .Q(register_6_q), .clr(1'b0));
  Register #(.width(32)) register_7 (
    .D(WriteData), .en(demultiplexer_1_out6), .clk(Clock), .Q(register_7_q), .clr(1'b0));
  Register #(.width(32)) register_8 (
    .D(WriteData), .en(demultiplexer_1_out7), .clk(Clock), .Q(register_8_q), .clr(1'b0));
  Register #(.width(32)) register_9 (
    .D(WriteData), .en(demultiplexer_1_out8), .clk(Clock), .Q(register_9_q), .clr(1'b0));
  Register #(.width(32)) register_10 (
    .D(WriteData), .en(demultiplexer_1_out9), .clk(Clock), .Q(register_10_q), .clr(1'b0));
  Register #(.width(32)) register_11 (
    .D(WriteData), .en(demultiplexer_1_out10), .clk(Clock), .Q(register_11_q), .clr(1'b0));
  Register #(.width(32)) register_12 (
    .D(WriteData), .en(demultiplexer_1_out11), .clk(Clock), .Q(register_12_q), .clr(1'b0));
  Register #(.width(32)) register_13 (
    .D(WriteData), .en(demultiplexer_1_out12), .clk(Clock), .Q(register_13_q), .clr(1'b0));
  Register #(.width(32)) register_14 (
    .D(WriteData), .en(demultiplexer_1_out13), .clk(Clock), .Q(register_14_q), .clr(1'b0));
  Register #(.width(32)) register_15 (
    .D(WriteData), .en(demultiplexer_1_out14), .clk(Clock), .Q(register_15_q), .clr(1'b0));
  Register #(.width(32)) register_16 (
    .D(WriteData), .en(demultiplexer_1_out15), .clk(Clock), .Q(register_16_q), .clr(1'b0));
  Register #(.width(32)) register_17 (
    .D(WriteData), .en(demultiplexer_1_out16), .clk(Clock), .Q(register_17_q), .clr(1'b0));
  Register #(.width(32)) register_18 (
    .D(WriteData), .en(demultiplexer_1_out17), .clk(Clock), .Q(register_18_q), .clr(1'b0));
  Register #(.width(32)) register_19 (
    .D(WriteData), .en(demultiplexer_1_out18), .clk(Clock), .Q(register_19_q), .clr(1'b0));
  Register #(.width(32)) register_20 (
    .D(WriteData), .en(demultiplexer_1_out19), .clk(Clock), .Q(register_20_q), .clr(1'b0));
  Register #(.width(32)) register_21 (
    .D(WriteData), .en(demultiplexer_1_out20), .clk(Clock), .Q(register_21_q), .clr(1'b0));
  Register #(.width(32)) register_22 (
    .D(WriteData), .en(demultiplexer_1_out21), .clk(Clock), .Q(register_22_q), .clr(1'b0));
  Register #(.width(32)) register_23 (
    .D(WriteData), .en(demultiplexer_1_out22), .clk(Clock), .Q(register_23_q), .clr(1'b0));
  Register #(.width(32)) register_24 (
    .D(WriteData), .en(demultiplexer_1_out23), .clk(Clock), .Q(register_24_q), .clr(1'b0));
  Register #(.width(32)) register_25 (
    .D(WriteData), .en(demultiplexer_1_out24), .clk(Clock), .Q(register_25_q), .clr(1'b0));
  Register #(.width(32)) register_26 (
    .D(WriteData), .en(demultiplexer_1_out25), .clk(Clock), .Q(register_26_q), .clr(1'b0));
  Register #(.width(32)) register_27 (
    .D(WriteData), .en(demultiplexer_1_out26), .clk(Clock), .Q(register_27_q), .clr(1'b0));
  Register #(.width(32)) register_28 (
    .D(WriteData), .en(demultiplexer_1_out27), .clk(Clock), .Q(register_28_q), .clr(1'b0));
  Register #(.width(32)) register_29 (
    .D(WriteData), .en(demultiplexer_1_out28), .clk(Clock), .Q(register_29_q), .clr(1'b0));
  Register #(.width(32)) register_30 (
    .D(WriteData), .en(demultiplexer_1_out29), .clk(Clock), .Q(register_30_q), .clr(1'b0));
  Register #(.width(32)) register_31 (
    .D(WriteData), .en(demultiplexer_1_out30), .clk(Clock), .Q(register_31_q), .clr(1'b0));
  Register #(.width(32)) register_32 (
    .D(WriteData), .en(demultiplexer_1_out31), .clk(Clock), .Q(register_32_q), .clr(1'b0));
  Multiplexer #(.select(5), .width(32), .enable("false")) multiplexer_1 (
    .in0(register_1_q), .in1(register_2_q), .in2(register_3_q), .in3(register_4_q), .in4(register_5_q),
    .in5(register_6_q), .in6(register_7_q), .in7(register_8_q), .in8(register_9_q), .in9(register_10_q),
    .in10(register_11_q), .in11(register_12_q), .in12(register_13_q), .in13(register_14_q),
    .in14(register_15_q), .in15(register_16_q), .in16(register_17_q), .in17(register_18_q),
    .in18(register_19_q), .in19(register_20_q), .in20(register_21_q), .in21(register_22_q),
    .in22(register_23_q), .in23(register_24_q), .in24(register_25_q), .in25(register_26_q),
    .in26(register_27_q), .in27(register_28_q), .in28(register_29_q), .in29(register_30_q),
    .in30(register_31_q), .in31(register_32_q), .out(ReadData1), .sel(ReadRegister1));
  Multiplexer #(.select(5), .width(32), .enable("false")) multiplexer_2 (
    .in0(register_1_q), .in1(register_2_q), .in2(register_3_q), .in3(register_4_q), .in4(register_5_q),
    .in5(register_6_q), .in6(register_7_q), .in7(register_8_q), .in8(register_9_q), .in9(register_10_q),
    .in10(register_11_q), .in11(register_12_q), .in12(register_13_q), .in13(register_14_q),
    .in14(register_15_q), .in15(register_16_q), .in16(register_17_q), .in17(register_18_q),
    .in18(register_19_q), .in19(register_20_q), .in20(register_21_q), .in21(register_22_q),
    .in22(register_23_q), .in23(register_24_q), .in24(register_25_q), .in25(register_26_q),
    .in26(register_27_q), .in27(register_28_q), .in28(register_29_q), .in29(register_30_q),
    .in30(register_31_q), .in31(register_32_q), .out(ReadData2), .sel(ReadRegister2));
endmodule

module trab3 (
  input  Clk
);

  wire AluSRC, and_1_out, Branch, Jal, Jump, JumpRegister, MemRead, MemtoReg, MemWrite, RegDst, RegWrite,
       trab2_alu_1_zero;
  wire [1:0] WHB;
  wire [2:0] ALU_op;
  wire [4:0] multiplexer_1_out, multiplexer_2_out;
  wire [5:0] trab1_datapath_1_datapath_out_2, trab4_alu_control_1_alu_code;
  wire [9:0] trab1_datapath_1_datapath_out_3;
  wire [27:0] trab5_shiftleft2_28_1_sh_out;
  wire [31:0] adder_1_out, multiplexer_3_out, multiplexer_4_out, multiplexer_5_out, multiplexer_6_out,
       multiplexer_7_out, multiplexer_8_out, trab1_datapath_1_add_out, trab2_alu_1_outpt,
       trab2_registers_1_readdata1, trab2_registers_1_readdata2, trab3_datamemory_1_data,
       trab3_shiftleft2_32_1_sh_out, trab3_signal_extender_1_out_32;
  wire [31:16] trab1_datapath_1_datapath_out;

  // Probe on multiplexer_5_out
  trab1_Datapath trab1_datapath_1 (
    .PC(multiplexer_5_out), .ck(Clk), .add_out(trab1_datapath_1_add_out),
    .datapath_out({trab1_datapath_1_datapath_out, trab1_datapath_1_datapath_out_3, trab1_datapath_1_datapath_out_2}));
  // Probe on {trab1_datapath_1_datapath_out, trab1_datapath_1_datapath_out_3, trab1_datapath_1_datapath_out_2}
  trab5_ShiftLeft2_28 trab5_shiftleft2_28_1 (
    .Sh_out(trab5_shiftleft2_28_1_sh_out),
    .Sh_in({trab1_datapath_1_datapath_out[25:16], trab1_datapath_1_datapath_out_3, trab1_datapath_1_datapath_out_2}));
  trab4_Control trab4_control_1 (
    .OP_code({trab1_datapath_1_datapath_out[26], trab1_datapath_1_datapath_out[27], trab1_datapath_1_datapath_out[28], trab1_datapath_1_datapath_out[29], trab1_datapath_1_datapath_out[30], trab1_datapath_1_datapath_out[31]}),
    .RegDst(RegDst), .Branch(Branch), .MemRead(MemRead), .MemtoReg(MemtoReg), .MemWrite(MemWrite),
    .AluSRC(AluSRC), .RegWrite(RegWrite), .AluOP(ALU_op), .WHB(WHB), .Jump(Jump), .Jal(Jal));
  Multiplexer #(.width(5), .enable("false")) multiplexer_1 (
    .in0(trab1_datapath_1_datapath_out[20:16]), .in1(trab1_datapath_1_datapath_out_3[9:5]),
    .out(multiplexer_1_out), .sel(RegDst));
  // Probe on trab1_datapath_1_datapath_out_3[9:5]
  Multiplexer #(.width(5), .enable("false")) multiplexer_2 (
    .in0(multiplexer_1_out), .in1({5{1'b1}}), .out(multiplexer_2_out), .sel(Jal));
  // Probe on trab1_datapath_1_datapath_out[25:21]
  // Probe on trab1_datapath_1_datapath_out[20:16]
  // Probe on trab1_datapath_1_datapath_out_2
  // Probe on {trab1_datapath_1_datapath_out_3, trab1_datapath_1_datapath_out_2}
  // Probe on trab2_registers_1_readdata1
  trab2_Registers trab2_registers_1 (
    .ReadData1(trab2_registers_1_readdata1), .Write(RegWrite),
    .ReadRegister1(trab1_datapath_1_datapath_out[25:21]),
    .ReadRegister2(trab1_datapath_1_datapath_out[20:16]), .Clock(Clk), .WriteRegister(multiplexer_2_out),
    .WriteData(multiplexer_8_out), .ReadData2(trab2_registers_1_readdata2));
  // Probe on trab2_registers_1_readdata2
  trab3_Signal_Extender trab3_signal_extender_1 (
    .out_32(trab3_signal_extender_1_out_32),
    .in_16({trab1_datapath_1_datapath_out_3, trab1_datapath_1_datapath_out_2}));
  Multiplexer #(.width(32), .enable("false")) multiplexer_3 (
    .in0(trab2_registers_1_readdata2), .in1(trab3_signal_extender_1_out_32), .out(multiplexer_3_out),
    .sel(AluSRC));
  // Probe on trab3_signal_extender_1_out_32
  trab4_ALU_control trab4_alu_control_1 (
    .Instruction(trab1_datapath_1_datapath_out_2), .ALU_op(ALU_op), .ALU_code(trab4_alu_control_1_alu_code),
    .JumpRegitster(JumpRegister));
  trab3_ShiftLeft2_32 trab3_shiftleft2_32_1 (
    .Sh_out(trab3_shiftleft2_32_1_sh_out), .Sh_in(trab3_signal_extender_1_out_32));
  // Probe on trab4_alu_control_1_alu_code
  // Probe on trab3_shiftleft2_32_1_sh_out
  Adder #(.width(32)) adder_1 (
    .a(trab1_datapath_1_add_out), .b(trab3_shiftleft2_32_1_sh_out), .out(adder_1_out), .cin(1'b0));  // open: cout
  and and_1 (and_1_out, Branch, trab2_alu_1_zero);
  trab2_ALU trab2_alu_1 (
    .Outpt(trab2_alu_1_outpt), .In2(multiplexer_3_out), .ALU_ctrl(trab4_alu_control_1_alu_code),
    .In1(trab2_registers_1_readdata1), .Zero(trab2_alu_1_zero));
  // Probe on adder_1_out
  // Probe on trab2_alu_1_outpt
  Multiplexer #(.width(32), .enable("false")) multiplexer_4 (
    .in0(trab1_datapath_1_add_out), .in1(adder_1_out), .out(multiplexer_4_out), .sel(and_1_out));
  Multiplexer #(.width(32), .enable("false")) multiplexer_5 (
    .in0(multiplexer_6_out), .in1(trab2_registers_1_readdata1), .out(multiplexer_5_out), .sel(JumpRegister));
  Multiplexer #(.width(32), .enable("false")) multiplexer_6 (
    .in0(multiplexer_4_out), .in1({trab1_datapath_1_add_out[31:28], trab5_shiftleft2_28_1_sh_out}),
    .out(multiplexer_6_out), .sel(Jump));
  // Probe on multiplexer_8_out
  // Probe on trab3_datamemory_1_data
  trab3_DataMemory trab3_datamemory_1 (
    .Address(trab2_alu_1_outpt), .WHB(WHB), .WriteData(trab2_registers_1_readdata2), .MemWrite(MemWrite),
    .MemRead(MemRead), .Clock(Clk), .Data(trab3_datamemory_1_data));
  Multiplexer #(.width(32), .enable("false")) multiplexer_7 (
    .in0(trab2_alu_1_outpt), .in1(trab3_datamemory_1_data), .out(multiplexer_7_out), .sel(MemtoReg));
  Multiplexer #(.width(32), .enable("false")) multiplexer_8 (
    .in0(multiplexer_7_out), .in1(trab1_datapath_1_add_out), .out(multiplexer_8_out), .sel(Jal));

  // Notes on the sheet:
  //   fio potencialmente errado
endmodule

module trab3_ShiftLeft2_32 (
  input  [31:0] Sh_in,
  output [31:0] Sh_out
);


  assign Sh_out = {Sh_in[29:0], 2'b00};
endmodule

module trab3_DataMemory (
  input  [31:0] Address,
  input  [1:0] WHB,
  input  [31:0] WriteData,
  input  MemWrite,
  input  MemRead,
  input  Clock,
  output [31:0] Data
);

  wire [1:0] demultiplexer_4_out0, demultiplexer_4_out1;
  wire [3:0] demultiplexer_5_out0, multiplexer_2_out;
  wire [7:0] demultiplexer_2_out0, demultiplexer_2_out1, demultiplexer_2_out2, demultiplexer_2_out3,
       multiplexer_4_out, ram_1_dout, ram_2_dout, ram_3_dout, ram_4_dout;
  wire [15:0] demultiplexer_3_out0, demultiplexer_3_out1, multiplexer_3_out;
  wire [31:0] demultiplexer_1_out0, demultiplexer_1_out1, demultiplexer_1_out2, multiplexer_1_out;

  Demultiplexer #(.select(2), .width(32), .enable("false")) demultiplexer_1 (
    .out0(demultiplexer_1_out0), .out1(demultiplexer_1_out1), .out2(demultiplexer_1_out2), .in(WriteData),
    .sel(WHB));  // open: out3
  Demultiplexer #(.select(2), .width(8), .enable("false")) demultiplexer_2 (
    .out0(demultiplexer_2_out0), .out1(demultiplexer_2_out1), .out2(demultiplexer_2_out2),
    .out3(demultiplexer_2_out3), .in(demultiplexer_1_out2[7:0]), .sel({Address[0], Address[1]}));
  Demultiplexer #(.width(16), .enable("false")) demultiplexer_3 (
    .out0(demultiplexer_3_out0), .out1(demultiplexer_3_out1), .in(demultiplexer_1_out1[15:0]),
    .sel(Address[1]));
  Demultiplexer #(.width(2), .enable("false")) demultiplexer_4 (
    .out0(demultiplexer_4_out0), .out1(demultiplexer_4_out1), .in({2{MemWrite}}), .sel(Address[1]));
  Demultiplexer #(.select(2), .enable("false")) demultiplexer_5 (
    .out0(demultiplexer_5_out0[0]), .out1(demultiplexer_5_out0[1]), .out2(demultiplexer_5_out0[2]),
    .out3(demultiplexer_5_out0[3]), .in(MemWrite), .sel(Address[1:0]));
  Multiplexer #(.select(2), .width(32), .enable("false")) multiplexer_1 (
    .in0(demultiplexer_1_out0), .in1({demultiplexer_3_out1, demultiplexer_3_out0}),
    .in2({demultiplexer_2_out3, demultiplexer_2_out2, demultiplexer_2_out1, demultiplexer_2_out0}),
    .in3({32{1'b0}}), .out(multiplexer_1_out), .sel(WHB));
  Multiplexer #(.select(2), .width(4), .enable("false")) multiplexer_2 (
    .in0({4{MemWrite}}), .in1({demultiplexer_4_out1, demultiplexer_4_out0}), .in2(demultiplexer_5_out0),
    .in3(4'b0000), .out(multiplexer_2_out), .sel(WHB));
  RAM #(.addrWidth(24), .trigger("falling"), .databus("bibus")) ram_1 (
    .addr(Address[25:2]), .we(multiplexer_2_out[0]), .oe(MemRead), .clk(Clock), .din(multiplexer_1_out[7:0]),
    .dout(ram_1_dout));
  RAM #(.addrWidth(24), .trigger("falling"), .databus("bibus")) ram_2 (
    .addr(Address[25:2]), .we(multiplexer_2_out[1]), .oe(MemRead), .clk(Clock),
    .din(multiplexer_1_out[15:8]), .dout(ram_2_dout));
  RAM #(.addrWidth(24), .trigger("falling"), .databus("bibus")) ram_3 (
    .addr(Address[25:2]), .we(multiplexer_2_out[2]), .oe(MemRead), .clk(Clock),
    .din(multiplexer_1_out[23:16]), .dout(ram_3_dout));
  RAM #(.addrWidth(24), .trigger("falling"), .databus("bibus")) ram_4 (
    .addr(Address[25:2]), .we(multiplexer_2_out[3]), .oe(MemRead), .clk(Clock),
    .din(multiplexer_1_out[31:24]), .dout(ram_4_dout));
  Multiplexer #(.width(16), .enable("false")) multiplexer_3 (
    .in0({ram_2_dout, ram_1_dout}), .in1({ram_4_dout, ram_3_dout}), .out(multiplexer_3_out), .sel(Address[1]));
  Multiplexer #(.select(2), .width(8), .enable("false")) multiplexer_4 (
    .in0(ram_1_dout), .in1(ram_2_dout), .in2(ram_3_dout), .in3(ram_4_dout), .out(multiplexer_4_out),
    .sel(Address[1:0]));
  Multiplexer #(.select(2), .width(32), .enable("false")) multiplexer_5 (
    .in0({ram_4_dout, ram_3_dout, ram_2_dout, ram_1_dout}), .in1({{16{1'b0}}, multiplexer_3_out}),
    .in2({{24{1'b0}}, multiplexer_4_out}), .in3({32{1'b0}}), .out(Data), .sel(WHB));
endmodule

module trab3_Signal_Extender (
  input  [15:0] in_16,
  output [31:0] out_32
);


  assign out_32 = {{17{in_16[15]}}, in_16[14:0]};
endmodule

module trab3_ShiftLeft2 (
  input  [31:0] Sh_in,
  output [31:0] Sh_out
);


  assign Sh_out = {Sh_in[29:0], 2'b00};
endmodule

module trab4_ALU_control (
  input  [5:0] Instruction,
  input  [2:0] ALU_op,
  output [5:0] ALU_code,
  output JumpRegitster
);

  wire and_1_out, and_2_out, not_1_out, not_2_out, not_3_out, not_4_out, not_5_out, not_6_out, not_7_out,
       not_8_out;

  Multiplexer #(.select(3), .width(6), .enable("false")) multiplexer_1 (
    .in0(Instruction), .in1({6{1'b0}}), .in2(6'b000100), .in3(6'b000101), .in4(6'b000011), .in5(6'b001001),
    .in6(6'b000110), .in7(6'b001000), .out(ALU_code), .sel(ALU_op));
  not not_1 (not_1_out, ALU_code[0]);
  not not_2 (not_2_out, ALU_code[1]);
  not not_3 (not_3_out, ALU_code[2]);
  not not_4 (not_4_out, ALU_code[4]);
  not not_5 (not_5_out, ALU_code[5]);
  not not_6 (not_6_out, ALU_op[0]);
  not not_7 (not_7_out, ALU_op[1]);
  not not_8 (not_8_out, ALU_op[2]);
  and and_1 (and_1_out, not_1_out, not_2_out, not_3_out, ALU_code[3], not_4_out, not_5_out);
  and and_2 (and_2_out, not_6_out, not_7_out, not_8_out);
  and and_3 (JumpRegitster, and_1_out, and_2_out);
endmodule

module trab4_Control (
  input  [5:0] OP_code,
  output RegDst,
  output Branch,
  output MemRead,
  output MemtoReg,
  output MemWrite,
  output AluSRC,
  output RegWrite,
  output [2:0] AluOP,
  output [1:0] WHB,
  output Jump,
  output Jal
);

  wire [15:14] rom_1_data;

  ROM #(.addrWidth(6), .dataWidth(16)) rom_1 (
    .addr(OP_code),
    .data({rom_1_data, Jal, Jump, WHB, AluOP, RegWrite, AluSRC, MemWrite, MemtoReg, MemRead, Branch, RegDst}));

  // Notes on the sheet:
  //   contents of rom_1 (hex, n*v repeats v):
  //   41 0 0 0 e0 8b0 0 0 202 8ec 0 0 160 0 0 0 1000 17*0 16c 0 e0 4b0 0 0 382 4ec 0 0 1e0 0 0 0 3040 ec 0
  //   0 0 b0 6*0 2e0
endmodule

module trab4_LoadUpper (
  input  [31:0] in_1,
  output [31:0] out_2
);


  assign out_2 = {in_1[15:0], {16{1'b0}}};
endmodule

module trab5_ShiftLeft2_28 (
  input  [25:0] Sh_in,
  output [27:0] Sh_out
);


  assign Sh_out = {Sh_in, 2'b00};
endmodule

module trab2_ALU (
  input  [5:0] ALU_ctrl,
  input  [31:0] In1,
  input  [31:0] In2,
  output Zero,
  output [31:0] Outpt
);

  wire comparator_1_eq, or_2_out;
  wire [31:0] adder_1_out, and_1_out, bit_extender_1_out, nor_1_out, or_1_out, subtractor_1_out,
       trab4_loadupper_1_out_2, xor_1_out;

  Adder #(.width(32)) adder_1 (.a(In1), .b(In2), .out(adder_1_out), .cin(1'b0));  // open: cout
  Subtractor #(.width(32)) subtractor_1 (.a(In1), .b(In2), .out(subtractor_1_out), .bin(1'b0));  // open: bout
  assign and_1_out = In1 & In2;  // AND_Gate and_1, 32 bits wide
  assign or_1_out = In1 | In2;  // OR_Gate or_1, 32 bits wide
  assign xor_1_out = In1 ^ In2;  // XOR_Gate xor_1, 32 bits wide
  assign nor_1_out = ~(In1 | In2);  // NOR_Gate nor_1, 32 bits wide
  assign bit_extender_1_out = {{31{comparator_1_eq}}, comparator_1_eq};  // Bit_Extender bit_extender_1
  Comparator #(.width(32)) comparator_1 (.a(In1), .b(In2), .eq(comparator_1_eq));  // open: gt, lt
  trab4_LoadUpper trab4_loadupper_1 (.in_1(In2), .out_2(trab4_loadupper_1_out_2));
  Multiplexer #(.select(4), .width(32), .enable("false")) multiplexer_1 (
    .in0(adder_1_out), .in1(adder_1_out), .in2(subtractor_1_out), .in3(subtractor_1_out), .in4(and_1_out),
    .in5(or_1_out), .in6(xor_1_out), .in7(nor_1_out), .in8(bit_extender_1_out),
    .in9(trab4_loadupper_1_out_2), .in10({32{1'b0}}), .in11({32{1'b0}}), .in12({32{1'b0}}),
    .in13({32{1'b0}}), .in14({32{1'b0}}), .in15({32{1'b0}}), .out(Outpt), .sel(ALU_ctrl[3:0]));
  // Probe on ALU_ctrl[3:0]
  or or_2 (or_2_out, Outpt[15], Outpt[0], Outpt[1], Outpt[2], Outpt[3], Outpt[4], Outpt[5], Outpt[6], Outpt[7], Outpt[8], Outpt[9], Outpt[10], Outpt[11], Outpt[12], Outpt[13], Outpt[14], Outpt[16], Outpt[17], Outpt[18], Outpt[19], Outpt[20], Outpt[21], Outpt[22], Outpt[23], Outpt[24], Outpt[25], Outpt[26], Outpt[27], Outpt[28], Outpt[29], Outpt[30], Outpt[31]);
  not not_1 (Zero, or_2_out);

  // Notes on the sheet:
  //   add = addu
  //   sub = subu
endmodule
